# Fritzing sketch rpi3_schematics (saved by Fritzing 0.9.3b)
breadboards: 1

parts:
  Raspberry_Pi_1 = Raspberry Pi 3 [part_number=RPI-3-V1.2]
  Part3 = Adafruit_BMP280
  PIR2 = PIR sensor

nets:
  N1: Raspberry_Pi_1.GPIO2, Part3.SDI/SDA
  N2: Raspberry_Pi_1.GPIO3, Part3.SCK/SCL
  GND: Raspberry_Pi_1.GND, Part3.GND, PIR2.GND
  N3: Raspberry_Pi_1.GPIO21, PIR2.SIG
  5V: Raspberry_Pi_1.5V, Part3.VIN, PIR2.VDD

custom parts:
  Adafruit_BMP280: Bosch has stepped up their game with their new BMP280 sensor, an environmental sensor with temperature, barometric pressure that is the next generation upgrade to the BMP085/BMP180/BMP183. This sensor is great for all sorts of weather sensing and can even be used in both I2C and SPI! This precision sensor from Bosch is the best low-cost, precision sensing solution for measuring barometric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
